// Logisim project PROJECT 2 DDCA LOGISM DIAGRAM.circ as structural Verilog: 1 circuit, main circuit main
module main (
  input  D,
  input  M,
  input  A,
  input  S,
  output \output 
);

  wire and_1_out, OR_out;

  or OR (OR_out, D, M);
  and and_1 (and_1_out, OR_out, A);
  or or_2 (\output , and_1_out, S);

  // Notes on the sheet:
  //   OR 1: D OR M
  //   ALARM = S PR [ A AND (D OR M) ]
  //   AND: A AND (D OR M)
  //   OR 2: AND OR S
endmodule
